// Logisim project 0_Fdecoder_switchable.circ as structural Verilog: 1 circuit, main circuit main
module main (
  input  [3:0] in_1
);

  wire and_1_out, and_2_out, and_3_out, decoder_1_out0, decoder_1_out1, decoder_1_out2, decoder_1_out3,
       decoder_1_out4, decoder_1_out5, decoder_1_out6, decoder_1_out7, decoder_1_out8, decoder_1_out9,
       decoder_1_out10, decoder_1_out11, decoder_1_out12, decoder_1_out13, decoder_1_out14, decoder_1_out15,
       dipswitch_1_sw1, not_1_out, or_1_out, or_2_out, or_3_out, or_4_out, or_5_out, or_6_out, or_7_out;

  DipSwitch #(.number(1)) dipswitch_1 (.sw1(dipswitch_1_sw1));
  not not_1 (not_1_out, dipswitch_1_sw1);
  Decoder #(.select(4)) decoder_1 (
    .out0(decoder_1_out0), .out1(decoder_1_out1), .out2(decoder_1_out2), .out3(decoder_1_out3),
    .out4(decoder_1_out4), .out5(decoder_1_out5), .out6(decoder_1_out6), .out7(decoder_1_out7),
    .out8(decoder_1_out8), .out9(decoder_1_out9), .out10(decoder_1_out10), .out11(decoder_1_out11),
    .out12(decoder_1_out12), .out13(decoder_1_out13), .out14(decoder_1_out14), .out15(decoder_1_out15),
    .sel(in_1), .en(1'b1));
  and and_1 (and_1_out, decoder_1_out11, not_1_out);
  and and_2 (and_2_out, decoder_1_out11, dipswitch_1_sw1);
  and and_3 (and_3_out, decoder_1_out11, dipswitch_1_sw1);
  or or_1 (or_1_out, decoder_1_out11, decoder_1_out10, decoder_1_out9, decoder_1_out7, decoder_1_out0, decoder_1_out3, decoder_1_out4, decoder_1_out1, decoder_1_out6, decoder_1_out8, decoder_1_out13, decoder_1_out5);
  or or_2 (or_2_out, and_2_out, decoder_1_out6, decoder_1_out9, decoder_1_out0, decoder_1_out3, decoder_1_out14, decoder_1_out5, decoder_1_out2, decoder_1_out8, decoder_1_out12, decoder_1_out13);
  or or_3 (or_3_out, decoder_1_out12, decoder_1_out11, decoder_1_out10, decoder_1_out0, decoder_1_out6, decoder_1_out8, decoder_1_out2, decoder_1_out13, decoder_1_out14, decoder_1_out15);
  or or_4 (or_4_out, decoder_1_out14, decoder_1_out15, decoder_1_out9, decoder_1_out0, decoder_1_out0, decoder_1_out3, decoder_1_out7, decoder_1_out5, decoder_1_out2, decoder_1_out6, decoder_1_out8, decoder_1_out12, decoder_1_out10);
  or or_5 (or_5_out, and_1_out, decoder_1_out13, decoder_1_out10, decoder_1_out8, decoder_1_out0, decoder_1_out2, decoder_1_out4, decoder_1_out3, decoder_1_out1, decoder_1_out7, decoder_1_out9);
  or or_6 (or_6_out, decoder_1_out15, decoder_1_out11, decoder_1_out10, decoder_1_out0, decoder_1_out5, decoder_1_out9, decoder_1_out6, decoder_1_out4, decoder_1_out8, decoder_1_out12, decoder_1_out14);
  or or_7 (or_7_out, decoder_1_out6, decoder_1_out14, decoder_1_out10, decoder_1_out9, decoder_1_out2, decoder_1_out4, decoder_1_out5, decoder_1_out3, decoder_1_out8, and_3_out, decoder_1_out13, decoder_1_out15);
  _7_Segment_Display u_7_segment_display_1 (
    .g(or_7_out), .f(or_6_out), .a(or_4_out), .b(or_5_out), .e(or_3_out), .d(or_2_out), .c(or_1_out));  // open: dp
endmodule
