// Logisim project 2_4decoder.circ as structural Verilog: 1 circuit, main circuit decoder_2to4
module decoder_2to4 (
  input  i0,
  input  i1,
  output o0,
  output o1,
  output o2,
  output o3
);

  wire not_1_out, not_2_out;

  not not_1 (not_1_out, i0);
  not not_2 (not_2_out, i1);
  and and_1 (o0, not_1_out, not_2_out);
  and and_2 (o1, i0, not_2_out);
  and and_3 (o2, not_1_out, i1);
  and and_4 (o3, i0, i1);

  // Notes on the sheet:
  //   0
  //   0
  //   0
  //   1
  //   2
  //   3
endmodule
