// Logisim project 4_16decoder.circ as structural Verilog: 3 circuits, main circuit decoder_4to16
module decoder_4to16 (
  input  i0,
  input  i1,
  input  i2,
  input  i3,
  output o0,
  output o1,
  output o2,
  output o3,
  output o4,
  output o5,
  output o6,
  output o7,
  output o8,
  output o9,
  output o10,
  output o11,
  output o12,
  output o13,
  output o14,
  output o15
);

  wire decoder_3to8_1_o0, decoder_3to8_1_o1, decoder_3to8_1_o2, decoder_3to8_1_o3, decoder_3to8_1_o4,
       decoder_3to8_1_o5, decoder_3to8_1_o6, decoder_3to8_1_o7, decoder_3to8_2_o0, decoder_3to8_2_o1,
       decoder_3to8_2_o2, decoder_3to8_2_o3, decoder_3to8_2_o4, decoder_3to8_2_o5, decoder_3to8_2_o6,
       decoder_3to8_2_o7, not_1_out;

  decoder_3to8 decoder_3to8_1 (
    .i0(i0), .i1(i1), .i3(i2), .o0(decoder_3to8_1_o0), .o1(decoder_3to8_1_o1), .o2(decoder_3to8_1_o2),
    .o3(decoder_3to8_1_o3), .o4(decoder_3to8_1_o4), .o5(decoder_3to8_1_o5), .o6(decoder_3to8_1_o6),
    .o7(decoder_3to8_1_o7));
  decoder_3to8 decoder_3to8_2 (
    .i0(i0), .i1(i1), .i3(i2), .o0(decoder_3to8_2_o0), .o1(decoder_3to8_2_o1), .o2(decoder_3to8_2_o2),
    .o3(decoder_3to8_2_o3), .o4(decoder_3to8_2_o4), .o5(decoder_3to8_2_o5), .o6(decoder_3to8_2_o6),
    .o7(decoder_3to8_2_o7));
  not not_1 (not_1_out, i3);
  and and_1 (o0, not_1_out, decoder_3to8_1_o0);
  and and_2 (o1, not_1_out, decoder_3to8_1_o1);
  and and_3 (o2, not_1_out, decoder_3to8_1_o2);
  and and_4 (o3, not_1_out, decoder_3to8_1_o3);
  and and_5 (o4, not_1_out, decoder_3to8_1_o4);
  and and_6 (o5, not_1_out, decoder_3to8_1_o5);
  and and_7 (o6, not_1_out, decoder_3to8_1_o6);
  and and_8 (o7, not_1_out, decoder_3to8_1_o7);
  and and_9 (o8, i3, decoder_3to8_2_o0);
  and and_10 (o9, i3, decoder_3to8_2_o1);
  and and_11 (o10, i3, decoder_3to8_2_o2);
  and and_12 (o11, i3, decoder_3to8_2_o3);
  and and_13 (o12, i3, decoder_3to8_2_o4);
  and and_14 (o13, i3, decoder_3to8_2_o5);
  and and_15 (o14, i3, decoder_3to8_2_o6);
  and and_16 (o15, i3, decoder_3to8_2_o7);
endmodule

module decoder_3to8 (
  input  i0,
  input  i1,
  input  i3,
  output o0,
  output o1,
  output o2,
  output o3,
  output o4,
  output o5,
  output o6,
  output o7
);

  wire decoder_2to4_1_o0, decoder_2to4_1_o1, decoder_2to4_1_o2, decoder_2to4_1_o3, decoder_2to4_2_o0,
       decoder_2to4_2_o1, decoder_2to4_2_o2, decoder_2to4_2_o3, not_1_out;

  decoder_2to4 decoder_2to4_1 (
    .i0(i0), .i1(i1), .o0(decoder_2to4_1_o0), .o1(decoder_2to4_1_o1), .o2(decoder_2to4_1_o2),
    .o3(decoder_2to4_1_o3));
  decoder_2to4 decoder_2to4_2 (
    .i0(i0), .i1(i1), .o0(decoder_2to4_2_o0), .o1(decoder_2to4_2_o1), .o2(decoder_2to4_2_o2),
    .o3(decoder_2to4_2_o3));
  and and_1 (o0, decoder_2to4_1_o0, not_1_out);
  and and_2 (o1, decoder_2to4_1_o1, not_1_out);
  and and_3 (o2, decoder_2to4_1_o2, not_1_out);
  and and_4 (o3, decoder_2to4_1_o3, not_1_out);
  and and_5 (o4, decoder_2to4_2_o0, i3);
  and and_6 (o5, decoder_2to4_2_o1, i3);
  and and_7 (o6, decoder_2to4_2_o2, i3);
  and and_8 (o7, decoder_2to4_2_o3, i3);
  not not_1 (not_1_out, i3);
  // AND_Gate and_9 is placed but not wired
endmodule

module decoder_2to4 (
  input  i0,
  input  i1,
  output o0,
  output o1,
  output o2,
  output o3
);

  wire not_1_out, not_2_out;

  not not_1 (not_1_out, i0);
  not not_2 (not_2_out, i1);
  and and_1 (o0, not_1_out, not_2_out);
  and and_2 (o1, i0, not_2_out);
  and and_3 (o2, not_1_out, i1);
  and and_4 (o3, i0, i1);

  // Notes on the sheet:
  //   0
  //   0
  //   0
  //   1
  //   2
  //   3
endmodule
