// Logisim project 4_1mux3bit.circ as structural Verilog: 1 circuit, main circuit main
module main (
  input  [2:0] I0,
  input  [2:0] in_2,
  input  [2:0] in_3,
  input  [2:0] in_4,
  input  [1:0] in_5,
  output [2:0] out_6
);

  wire decoder_2to4_1_o0, decoder_2to4_1_o1, decoder_2to4_1_o2, decoder_2to4_1_o3;
  wire [2:0] and_1_out, and_4_out, and_7_out, and_10_out;

  decoder_2to4 decoder_2to4_1 (
    .i0(in_5[0]), .i1(in_5[1]), .o0(decoder_2to4_1_o0), .o1(decoder_2to4_1_o1), .o2(decoder_2to4_1_o2),
    .o3(decoder_2to4_1_o3));
  and and_1 (and_1_out[0], I0[0], decoder_2to4_1_o0);
  and and_2 (and_1_out[1], I0[1], decoder_2to4_1_o0);
  and and_3 (and_1_out[2], I0[2], decoder_2to4_1_o0);
  and and_4 (and_4_out[0], in_2[0], decoder_2to4_1_o1);
  and and_5 (and_4_out[1], in_2[1], decoder_2to4_1_o1);
  and and_6 (and_4_out[2], in_2[2], decoder_2to4_1_o1);
  and and_7 (and_7_out[0], in_3[0], decoder_2to4_1_o2);
  and and_8 (and_7_out[1], in_3[1], decoder_2to4_1_o2);
  and and_9 (and_7_out[2], in_3[2], decoder_2to4_1_o2);
  and and_10 (and_10_out[0], in_4[0], decoder_2to4_1_o3);
  and and_11 (and_10_out[1], in_4[1], decoder_2to4_1_o3);
  and and_12 (and_10_out[2], in_4[2], decoder_2to4_1_o3);
  assign out_6 = and_1_out | and_4_out | and_7_out | and_10_out;  // OR_Gate or_1, 3 bits wide
endmodule
