// Logisim project 4bitadder.circ as structural Verilog: 1 circuit, main circuit main
module main (
  input  [3:0] a,
  input  [3:0] b,
  input  cin,
  output overflow,
  output cout,
  output [3:0] out_6
);

  wire and_1_out, and_2_out, bcd_to_7_segment_decoder_1_p1, bcd_to_7_segment_decoder_1_p2,
       bcd_to_7_segment_decoder_1_p3, bcd_to_7_segment_decoder_1_p4, bcd_to_7_segment_decoder_1_p6,
       bcd_to_7_segment_decoder_1_p7, bcd_to_7_segment_decoder_1_p8, fulladder_1_cout, fulladder_2_cout,
       fulladder_3_cout, not_1_out, not_2_out, not_3_out;

  fulladder fulladder_1 (.a(a[0]), .b(b[0]), .cin(cin), .cout(fulladder_1_cout), .s(out_6[0]));
  fulladder fulladder_2 (.a(a[1]), .b(b[1]), .cin(fulladder_1_cout), .cout(fulladder_2_cout), .s(out_6[1]));
  fulladder fulladder_3 (.a(a[2]), .b(b[2]), .cin(fulladder_2_cout), .cout(fulladder_3_cout), .s(out_6[2]));
  fulladder fulladder_4 (.a(a[3]), .b(b[3]), .cin(fulladder_3_cout), .cout(cout), .s(out_6[3]));
  not not_1 (not_1_out, a[3]);
  not not_2 (not_2_out, b[3]);
  not not_3 (not_3_out, out_6[3]);
  and and_1 (and_1_out, not_1_out, out_6[3], not_2_out);
  and and_2 (and_2_out, b[3], not_3_out, a[3]);
  LED led_1 (.in(cout));
  or or_1 (overflow, and_1_out, and_2_out);
  // BCD_to_7_Segment_decoder bcd_to_7_segment_decoder_1: pin names not known; wires that end beside it: bcd_to_7_segment_decoder_1_p1, bcd_to_7_segment_decoder_1_p2, bcd_to_7_segment_decoder_1_p3, bcd_to_7_segment_decoder_1_p4, out_6, bcd_to_7_segment_decoder_1_p6, bcd_to_7_segment_decoder_1_p7, bcd_to_7_segment_decoder_1_p8
  _7_Segment_Display u_7_segment_display_1 (
    .g(bcd_to_7_segment_decoder_1_p1), .f(bcd_to_7_segment_decoder_1_p3), .a(bcd_to_7_segment_decoder_1_p6),
    .b(bcd_to_7_segment_decoder_1_p8), .e(bcd_to_7_segment_decoder_1_p2), .d(bcd_to_7_segment_decoder_1_p4),
    .c(bcd_to_7_segment_decoder_1_p7));  // open: dp
endmodule
