// Logisim project 4bitscomparator.circ as structural Verilog: 1 circuit, main circuit main
module main (
  output out_1
);

  wire dipswitch_1_p1, dipswitch_1_p2, dipswitch_1_p3, dipswitch_1_p4, dipswitch_2_p1, dipswitch_2_p2,
       dipswitch_2_p3, dipswitch_2_p4, not_1_out, not_2_out, not_3_out, not_4_out, xor_1_out, xor_2_out,
       xor_3_out, xor_4_out;

  // DipSwitch #(.number(4)) dipswitch_1: pin names not known; wires that end beside it: dipswitch_1_p1, dipswitch_1_p2, dipswitch_1_p3, dipswitch_1_p4
  // DipSwitch #(.number(4)) dipswitch_2: pin names not known; wires that end beside it: dipswitch_2_p1, dipswitch_2_p2, dipswitch_2_p3, dipswitch_2_p4
  xor xor_1 (xor_1_out, dipswitch_1_p1, dipswitch_2_p1);
  xor xor_2 (xor_2_out, dipswitch_1_p2, dipswitch_2_p2);
  xor xor_3 (xor_3_out, dipswitch_1_p3, dipswitch_2_p3);
  xor xor_4 (xor_4_out, dipswitch_1_p4, dipswitch_2_p4);
  not not_1 (not_1_out, xor_2_out);
  not not_2 (not_2_out, xor_1_out);
  not not_3 (not_3_out, xor_3_out);
  not not_4 (not_4_out, xor_4_out);
  and and_1 (out_1, not_2_out, not_1_out, not_3_out, not_4_out);
  LED led_1 (.in(out_1));
endmodule
