// Logisim project 4bitsub.circ as structural Verilog: 3 circuits, main circuit main
module main (
  input  [3:0] a,
  input  [3:0] b,
  input  cin,
  output out_4,
  output [3:0] out_5
);

  wire fullsub_1_cout, fullsub_2_cout, fullsub_3_cout;

  fullsub fullsub_1 (.a(a[0]), .b(b[0]), .cin(cin), .cout(fullsub_1_cout), .sub(out_5[0]));
  fullsub fullsub_2 (.a(a[1]), .b(b[1]), .cin(fullsub_1_cout), .cout(fullsub_2_cout), .sub(out_5[1]));
  fullsub fullsub_3 (.a(a[2]), .b(b[2]), .cin(fullsub_2_cout), .cout(fullsub_3_cout), .sub(out_5[2]));
  fullsub fullsub_4 (.a(a[3]), .b(b[3]), .cin(fullsub_3_cout), .cout(out_4), .sub(out_5[3]));
endmodule

module halfsub (
  input  a,
  input  b,
  output sub,
  output c
);

  wire not_1_out;

  not not_1 (not_1_out, a);
  xor xor_1 (sub, a, b);
  and and_1 (c, not_1_out, b);
endmodule

module fullsub (
  input  a,
  input  b,
  input  cin,
  output cout,
  output sub
);

  wire halfsub_1_c, halfsub_1_sub, halfsub_2_c;

  halfsub halfsub_1 (.a(a), .b(b), .sub(halfsub_1_sub), .c(halfsub_1_c));
  halfsub halfsub_2 (.a(halfsub_1_sub), .b(cin), .sub(sub), .c(halfsub_2_c));
  or or_1 (cout, halfsub_1_c, halfsub_2_c);
endmodule
