// Logisim project 8bitadder.circ as structural Verilog: 1 circuit, main circuit adder8bit
module adder8bit (
  input  [7:0] a,
  input  [7:0] b,
  input  cin,
  output overflow,
  output cout,
  output [7:0] s
);

  wire adder4bit_1_cout;

  adder4bit adder4bit_1 (.a(a[3:0]), .b(b[3:0]), .cin(cin), .cout(adder4bit_1_cout), .s(s[3:0]));  // open: overflow
  adder4bit adder4bit_2 (.a(a[7:4]), .b(b[7:4]), .cin(adder4bit_1_cout), .overflow(overflow), .cout(cout), .s(s[7:4]));
endmodule
