// Logisim project 8bitdflipflop_en.circ as structural Verilog: 1 circuit, main circuit dflipflop_en_8bit
module dflipflop_en_8bit (
  input  [7:0] d,
  input  clk,
  input  en,
  input  reset,
  output [7:0] q,
  output [7:0] q_head
);

  dflipflop_en dflipflop_en_1 (.d(d[0]), .clk(clk), .en(en), .reset(reset), .q(q[0]), .q_head(q_head[0]));
  dflipflop_en dflipflop_en_2 (.d(d[1]), .clk(clk), .en(en), .reset(reset), .q(q[1]), .q_head(q_head[1]));
  dflipflop_en dflipflop_en_3 (.d(d[2]), .clk(clk), .en(en), .reset(reset), .q(q[2]), .q_head(q_head[2]));
  dflipflop_en dflipflop_en_4 (.d(d[3]), .clk(clk), .en(en), .reset(reset), .q(q[3]), .q_head(q_head[3]));
  dflipflop_en dflipflop_en_5 (.d(d[4]), .clk(clk), .en(en), .reset(reset), .q(q[4]), .q_head(q_head[4]));
  dflipflop_en dflipflop_en_6 (.d(d[5]), .clk(clk), .en(en), .reset(reset), .q(q[5]), .q_head(q_head[5]));
  dflipflop_en dflipflop_en_7 (.d(d[6]), .clk(clk), .en(en), .reset(reset), .q(q[6]), .q_head(q_head[6]));
  dflipflop_en dflipflop_en_8 (.d(d[7]), .clk(clk), .en(en), .reset(reset), .q(q[7]), .q_head(q_head[7]));
endmodule
