// Logisim project 8bitreg.circ as structural Verilog: 1 circuit, main circuit reg8bit
module reg8bit (
  input  [7:0] d,
  input  en,
  input  clk,
  input  reset,
  output [7:0] q
);

  reg4bit reg4bit_1 (.d(d[3:0]), .en(en), .clk(clk), .reset(reset), .q(q[3:0]));
  reg4bit reg4bit_2 (.d(d[7:4]), .en(en), .clk(clk), .reset(reset), .q(q[7:4]));
endmodule
