// Logisim project PriorityEncoder.circ as structural Verilog: 1 circuit, main circuit main
module main (
  input  I0,
  input  I1,
  input  I2,
  input  I3,
  output out_5,
  output out_6
);

  wire and_1_out, not_1_out, not_2_out;

  not not_1 (not_1_out, I3);
  not not_2 (not_2_out, I2);
  and and_1 (and_1_out, I1, not_1_out, not_2_out);
  or or_1 (out_5, and_1_out, I3);
  or or_2 (out_6, I2, I3);
endmodule
