// Logisim project counter4bit.circ as structural Verilog: 1 circuit, main circuit main
module main (
  input  en,
  input  clk,
  input  reset
);

  wire decoder0tof_1_a, decoder0tof_1_b, decoder0tof_1_c, decoder0tof_1_d, decoder0tof_1_dot,
       decoder0tof_1_e, decoder0tof_1_f, decoder0tof_1_g;
  wire [3:0] adder4bit_1_s, reg4bit_1_q;

  reg4bit reg4bit_1 (.d(adder4bit_1_s), .en(en), .clk(clk), .reset(reset), .q(reg4bit_1_q));
  adder4bit adder4bit_1 (.a(reg4bit_1_q), .b(4'b0001), .cin(1'b0), .s(adder4bit_1_s));  // open: overflow, cout
  decoder0toF decoder0tof_1 (
    .in_1(adder4bit_1_s), .a(decoder0tof_1_a), .b(decoder0tof_1_b), .dot(decoder0tof_1_dot),
    .c(decoder0tof_1_c), .d(decoder0tof_1_d), .e(decoder0tof_1_e), .f(decoder0tof_1_f), .g(decoder0tof_1_g));
  _7_Segment_Display u_7_segment_display_1 (
    .g(decoder0tof_1_g), .f(decoder0tof_1_f), .a(decoder0tof_1_a), .b(decoder0tof_1_b), .e(decoder0tof_1_e),
    .d(decoder0tof_1_d), .c(decoder0tof_1_c), .dp(decoder0tof_1_dot));
endmodule
