// Logisim project dflip_flop.circ as structural Verilog: 2 circuits, main circuit dflip_flop
module dflip_flop (
  input  d,
  input  clk,
  input  reset,
  output q,
  output q_head
);

  wire button_1_out, dlatch_1_q, not_1_out;

  Button button_1 (.out(button_1_out));
  not not_1 (not_1_out, clk);
  dlatch dlatch_1 (.d(d), .we(not_1_out), .reset(reset), .q(dlatch_1_q));  // open: q_head
  dlatch dlatch_2 (.d(dlatch_1_q), .we(clk), .reset(reset), .q(q), .q_head(q_head));

  // Notes on the sheet:
  //   reset: initial=0x1
endmodule

module reverse (
  input  in_1,
  input  in_2
);

  wire dflip_flop_1_q, not_1_out;

  dflip_flop dflip_flop_1 (.d(not_1_out), .clk(in_1), .reset(in_2), .q(dflip_flop_1_q));  // open: q_head
  not not_1 (not_1_out, dflip_flop_1_q);
endmodule
