// Logisim project dflip_flop_downedge.circ as structural Verilog: 1 circuit, main circuit main
module main (
  input  d,
  input  clk,
  input  reset,
  output q,
  output q_head
);

  wire button_1_out, dlatch_1_q, not_1_out;

  Button button_1 (.out(button_1_out));
  not not_1 (not_1_out, clk);
  dlatch dlatch_1 (.d(d), .we(clk), .reset(reset), .q(dlatch_1_q));  // open: q_head
  dlatch dlatch_2 (.d(dlatch_1_q), .we(not_1_out), .reset(reset), .q(q), .q_head(q_head));

  // Notes on the sheet:
  //   reset: initial=0x1
endmodule
