// Logisim project dflipflop_en.circ as structural Verilog: 1 circuit, main circuit dflipflop_en
module dflipflop_en (
  input  d,
  input  clk,
  input  en,
  input  reset,
  output q,
  output q_head
);

  wire not_1_out, or_1_out;

  not not_1 (not_1_out, en);
  or or_1 (or_1_out, clk, not_1_out);
  dflip_flop dflip_flop_1 (.d(d), .clk(or_1_out), .reset(reset), .q(q), .q_head(q_head));
endmodule
