// Logisim project digitclock.circ as structural Verilog: 1 circuit, main circuit main
module main (
  input  en,
  input  reset
);

  wire clk_out, comparator4bit_1_equal, comparator4bit_2_equal, comparator4bit_3_equal, decoder0to9_1_a,
       decoder0to9_1_b, decoder0to9_1_c, decoder0to9_1_d, decoder0to9_1_dot, decoder0to9_1_e,
       decoder0to9_1_f, decoder0to9_1_g, decoder0to9_2_a, decoder0to9_2_b, decoder0to9_2_c, decoder0to9_2_d,
       decoder0to9_2_dot, decoder0to9_2_e, decoder0to9_2_f, decoder0to9_2_g, decoder0to9_3_a,
       decoder0to9_3_b, decoder0to9_3_c, decoder0to9_3_d, decoder0to9_3_dot, decoder0to9_3_e,
       decoder0to9_3_f, decoder0to9_3_g, or_1_out, or_2_out, or_3_out;
  wire [3:0] adder4bit_1_s, adder4bit_2_s, adder4bit_3_s, reg4bit_1_q, reg4bit_2_q, reg4bit_3_q;

  Clock clk (.out(clk_out));
  or or_1 (or_1_out, reset, comparator4bit_1_equal);
  comparator4bit comparator4bit_1 (.a(4'b1010), .b(reg4bit_1_q), .equal(comparator4bit_1_equal));
  reg4bit reg4bit_1 (.d(adder4bit_1_s), .en(en), .clk(clk_out), .reset(or_1_out), .q(reg4bit_1_q));
  adder4bit adder4bit_1 (.a(reg4bit_1_q), .b(4'b0001), .cin(1'b0), .s(adder4bit_1_s));  // open: overflow, cout
  decoder0to9 decoder0to9_1 (
    .in_1(reg4bit_1_q), .a(decoder0to9_1_a), .b(decoder0to9_1_b), .dot(decoder0to9_1_dot),
    .c(decoder0to9_1_c), .d(decoder0to9_1_d), .e(decoder0to9_1_e), .f(decoder0to9_1_f), .g(decoder0to9_1_g));
  _7_Segment_Display u_7_segment_display_1 (
    .g(decoder0to9_1_g), .f(decoder0to9_1_f), .a(decoder0to9_1_a), .b(decoder0to9_1_b), .e(decoder0to9_1_e),
    .d(decoder0to9_1_d), .c(decoder0to9_1_c), .dp(decoder0to9_1_dot));
  or or_2 (or_2_out, reset, comparator4bit_2_equal);
  reg4bit reg4bit_2 (.d(adder4bit_2_s), .en(en), .clk(comparator4bit_1_equal), .reset(or_2_out), .q(reg4bit_2_q));
  comparator4bit comparator4bit_2 (.a(4'b0110), .b(reg4bit_2_q), .equal(comparator4bit_2_equal));
  adder4bit adder4bit_2 (.a(reg4bit_2_q), .b(4'b0001), .cin(1'b0), .s(adder4bit_2_s));  // open: overflow, cout
  decoder0to9 decoder0to9_2 (
    .in_1(reg4bit_2_q), .a(decoder0to9_2_a), .b(decoder0to9_2_b), .dot(decoder0to9_2_dot),
    .c(decoder0to9_2_c), .d(decoder0to9_2_d), .e(decoder0to9_2_e), .f(decoder0to9_2_f), .g(decoder0to9_2_g));
  _7_Segment_Display u_7_segment_display_2 (
    .g(decoder0to9_2_g), .f(decoder0to9_2_f), .a(decoder0to9_2_a), .b(decoder0to9_2_b), .e(decoder0to9_2_e),
    .d(decoder0to9_2_d), .c(decoder0to9_2_c), .dp(decoder0to9_2_dot));
  or or_3 (or_3_out, reset, comparator4bit_3_equal);
  reg4bit reg4bit_3 (.d(adder4bit_3_s), .en(en), .clk(comparator4bit_2_equal), .reset(or_3_out), .q(reg4bit_3_q));
  comparator4bit comparator4bit_3 (.a(4'b1010), .b(reg4bit_3_q), .equal(comparator4bit_3_equal));
  adder4bit adder4bit_3 (.a(reg4bit_3_q), .b(4'b0001), .cin(1'b0), .s(adder4bit_3_s));  // open: overflow, cout
  decoder0to9 decoder0to9_3 (
    .in_1(reg4bit_3_q), .a(decoder0to9_3_a), .b(decoder0to9_3_b), .dot(decoder0to9_3_dot),
    .c(decoder0to9_3_c), .d(decoder0to9_3_d), .e(decoder0to9_3_e), .f(decoder0to9_3_f), .g(decoder0to9_3_g));
  _7_Segment_Display u_7_segment_display_3 (
    .g(decoder0to9_3_g), .f(decoder0to9_3_f), .a(decoder0to9_3_a), .b(decoder0to9_3_b), .e(decoder0to9_3_e),
    .d(decoder0to9_3_d), .c(decoder0to9_3_c), .dp(decoder0to9_3_dot));
endmodule
