// Logisim project dlatch.circ as structural Verilog: 2 circuits, main circuit dlatch
module dlatch (
  input  d,
  input  we,
  input  reset,
  output q,
  output q_head
);

  wire and_1_out, and_2_out, multiplexer_1_out, multiplexer_2_out, not_1_out, or_1_out;

  not not_1 (not_1_out, d);
  or or_1 (or_1_out, we, reset);
  Multiplexer multiplexer_1 (.in0(d), .in1(1'b0), .out(multiplexer_1_out), .sel(reset));
  Multiplexer multiplexer_2 (.in0(not_1_out), .in1(1'b1), .out(multiplexer_2_out), .sel(reset));
  and and_1 (and_1_out, multiplexer_2_out, or_1_out);
  and and_2 (and_2_out, or_1_out, multiplexer_1_out);
  srlatch srlatch_1 (.r(and_1_out), .s(and_2_out), .q(q), .q_head(q_head));

  // Notes on the sheet:
  //   reset: initial=0x1
endmodule

module oscillation (
  input  in_1,
  input  in_2
);

  wire dlatch_1_q, not_1_out;

  dlatch dlatch_1 (.d(not_1_out), .we(in_1), .reset(in_2), .q(dlatch_1_q));  // open: q_head
  not not_1 (not_1_out, dlatch_1_q);
endmodule
