// Logisim project encoder.circ as structural Verilog: 1 circuit, main circuit main
module main (
);

  wire dipswitch_1_sw1, dipswitch_1_sw2, dipswitch_1_sw3, dipswitch_1_sw4, dipswitch_1_sw5, dipswitch_1_sw6,
       dipswitch_1_sw7, dipswitch_1_sw8, dipswitch_1_sw9, dipswitch_1_sw10, dipswitch_1_sw11,
       dipswitch_1_sw12, dipswitch_1_sw13, dipswitch_1_sw14, dipswitch_1_sw15, dipswitch_1_sw16, or_1_out,
       or_3_out, or_4_out, or_5_out, or_6_out, or_7_out, or_8_out;

  DipSwitch #(.number(16)) dipswitch_1 (
    .sw1(dipswitch_1_sw1), .sw2(dipswitch_1_sw2), .sw3(dipswitch_1_sw3), .sw4(dipswitch_1_sw4),
    .sw5(dipswitch_1_sw5), .sw6(dipswitch_1_sw6), .sw7(dipswitch_1_sw7), .sw8(dipswitch_1_sw8),
    .sw9(dipswitch_1_sw9), .sw10(dipswitch_1_sw10), .sw11(dipswitch_1_sw11), .sw12(dipswitch_1_sw12),
    .sw13(dipswitch_1_sw13), .sw14(dipswitch_1_sw14), .sw15(dipswitch_1_sw15), .sw16(dipswitch_1_sw16));
  or or_1 (or_1_out, dipswitch_1_sw12, dipswitch_1_sw11, dipswitch_1_sw10, dipswitch_1_sw8, dipswitch_1_sw1, dipswitch_1_sw4, dipswitch_1_sw5, dipswitch_1_sw2, dipswitch_1_sw7, dipswitch_1_sw9, dipswitch_1_sw14, dipswitch_1_sw6);
  // OR_Gate or_2 is placed but not wired
  or or_3 (or_3_out, dipswitch_1_sw12, dipswitch_1_sw7, dipswitch_1_sw10, dipswitch_1_sw1, dipswitch_1_sw4, dipswitch_1_sw15, dipswitch_1_sw6, dipswitch_1_sw3, dipswitch_1_sw9, dipswitch_1_sw13, dipswitch_1_sw14);
  or or_4 (or_4_out, dipswitch_1_sw13, dipswitch_1_sw12, dipswitch_1_sw11, dipswitch_1_sw1, dipswitch_1_sw7, dipswitch_1_sw9, dipswitch_1_sw3, dipswitch_1_sw14, dipswitch_1_sw15, dipswitch_1_sw16);
  or or_5 (or_5_out, dipswitch_1_sw15, dipswitch_1_sw16, dipswitch_1_sw10, dipswitch_1_sw1, dipswitch_1_sw1, dipswitch_1_sw4, dipswitch_1_sw8, dipswitch_1_sw6, dipswitch_1_sw3, dipswitch_1_sw7, dipswitch_1_sw9, dipswitch_1_sw13, dipswitch_1_sw11);
  or or_6 (or_6_out, dipswitch_1_sw14, dipswitch_1_sw11, dipswitch_1_sw9, dipswitch_1_sw1, dipswitch_1_sw3, dipswitch_1_sw5, dipswitch_1_sw4, dipswitch_1_sw2, dipswitch_1_sw8, dipswitch_1_sw10);
  or or_7 (or_7_out, dipswitch_1_sw16, dipswitch_1_sw12, dipswitch_1_sw11, dipswitch_1_sw1, dipswitch_1_sw6, dipswitch_1_sw10, dipswitch_1_sw7, dipswitch_1_sw5, dipswitch_1_sw9, dipswitch_1_sw13, dipswitch_1_sw15);
  or or_8 (or_8_out, dipswitch_1_sw7, dipswitch_1_sw15, dipswitch_1_sw11, dipswitch_1_sw10, dipswitch_1_sw3, dipswitch_1_sw5, dipswitch_1_sw6, dipswitch_1_sw4, dipswitch_1_sw9, dipswitch_1_sw12, dipswitch_1_sw14, dipswitch_1_sw16);
  _7_Segment_Display u_7_segment_display_1 (
    .g(or_8_out), .f(or_7_out), .a(or_5_out), .b(or_6_out), .e(or_4_out), .d(or_3_out), .c(or_1_out));  // open: dp
endmodule
