// Logisim project fulladder.circ as structural Verilog: 1 circuit, main circuit fulladder
module fulladder (
  input  a,
  input  b,
  input  cin,
  output cout,
  output s
);

  wire halfadder_1_c, halfadder_1_s, halfadder_2_c;

  halfadder halfadder_1 (.a(a), .b(b), .s(halfadder_1_s), .c(halfadder_1_c));
  halfadder halfadder_2 (.a(halfadder_1_s), .b(cin), .s(s), .c(halfadder_2_c));
  or or_1 (cout, halfadder_1_c, halfadder_2_c);
endmodule
