// Logisim project ram_4x8.circ as structural Verilog: 1 circuit, main circuit ram4x8
module ram4x8 (
  input  [7:0] d,
  input  [1:0] addr,
  input  en,
  input  clk,
  input  reset,
  output [7:0] o
);

  wire and_1_out, and_2_out, and_3_out, and_4_out, decoder_2to4_1_o0, decoder_2to4_1_o1, decoder_2to4_1_o2,
       decoder_2to4_1_o3, dflipflop_en_1_q, dflipflop_en_2_q, dflipflop_en_3_q, dflipflop_en_4_q,
       dflipflop_en_5_q, dflipflop_en_6_q, dflipflop_en_7_q, dflipflop_en_8_q, dflipflop_en_9_q,
       dflipflop_en_10_q, dflipflop_en_11_q, dflipflop_en_12_q, dflipflop_en_13_q, dflipflop_en_14_q,
       dflipflop_en_15_q, dflipflop_en_16_q, dflipflop_en_17_q, dflipflop_en_18_q, dflipflop_en_19_q,
       dflipflop_en_20_q, dflipflop_en_21_q, dflipflop_en_22_q, dflipflop_en_23_q, dflipflop_en_24_q,
       dflipflop_en_25_q, dflipflop_en_26_q, dflipflop_en_27_q, dflipflop_en_28_q, dflipflop_en_29_q,
       dflipflop_en_30_q, dflipflop_en_31_q, dflipflop_en_32_q, ram0_0, ram0_1, ram0_2, ram0_3, ram0_4,
       ram0_5, ram0_6, ram0_7, ram1_0, ram1_1, ram1_2, ram1_3, ram1_4, ram1_5, ram1_6, ram1_7, ram2_0,
       ram2_1, ram2_2, ram2_3, ram2_4, ram2_5, ram2_6, ram2_7, ram3_0, ram3_1, ram3_2, ram3_3, ram3_4,
       ram3_5, ram3_6, ram3_7;

  or or_1 (o[0], ram0_0, ram1_0, ram2_0, ram3_0);
  or or_2 (o[1], ram0_1, ram1_1, ram2_1, ram3_1);
  or or_3 (o[2], ram0_2, ram1_2, ram2_2, ram3_2);
  or or_4 (o[3], ram0_3, ram1_3, ram2_3, ram3_3);
  or or_5 (o[4], ram0_4, ram1_4, ram2_4, ram3_4);
  or or_6 (o[5], ram0_5, ram1_5, ram2_5, ram3_5);
  or or_7 (o[6], ram0_6, ram1_6, ram2_6, ram3_6);
  or or_8 (o[7], ram0_7, ram1_7, ram2_7, ram3_7);
  decoder_2to4 decoder_2to4_1 (
    .i0(addr[0]), .i1(addr[1]), .o0(decoder_2to4_1_o0), .o1(decoder_2to4_1_o1), .o2(decoder_2to4_1_o2),
    .o3(decoder_2to4_1_o3));
  and and_1 (and_1_out, decoder_2to4_1_o2, en);
  and and_2 (and_2_out, decoder_2to4_1_o0, en);
  and and_3 (and_3_out, decoder_2to4_1_o1, en);
  and and_4 (and_4_out, decoder_2to4_1_o3, en);
  dflipflop_en dflipflop_en_1 (
    .d(d[7]), .clk(clk), .en(and_2_out), .reset(reset), .q(dflipflop_en_1_q));  // open: q_head
  dflipflop_en dflipflop_en_2 (
    .d(d[7]), .clk(clk), .en(and_3_out), .reset(reset), .q(dflipflop_en_2_q));  // open: q_head
  dflipflop_en dflipflop_en_3 (
    .d(d[7]), .clk(clk), .en(and_1_out), .reset(reset), .q(dflipflop_en_3_q));  // open: q_head
  dflipflop_en dflipflop_en_4 (
    .d(d[7]), .clk(clk), .en(and_4_out), .reset(reset), .q(dflipflop_en_4_q));  // open: q_head
  and and_5 (ram2_7, decoder_2to4_1_o2, dflipflop_en_3_q);
  and and_6 (ram0_7, decoder_2to4_1_o0, dflipflop_en_1_q);
  and and_7 (ram1_7, decoder_2to4_1_o1, dflipflop_en_2_q);
  and and_8 (ram3_7, decoder_2to4_1_o3, dflipflop_en_4_q);
  dflipflop_en dflipflop_en_5 (
    .d(d[6]), .clk(clk), .en(and_2_out), .reset(reset), .q(dflipflop_en_5_q));  // open: q_head
  dflipflop_en dflipflop_en_6 (
    .d(d[6]), .clk(clk), .en(and_3_out), .reset(reset), .q(dflipflop_en_6_q));  // open: q_head
  dflipflop_en dflipflop_en_7 (
    .d(d[6]), .clk(clk), .en(and_1_out), .reset(reset), .q(dflipflop_en_7_q));  // open: q_head
  dflipflop_en dflipflop_en_8 (
    .d(d[6]), .clk(clk), .en(and_4_out), .reset(reset), .q(dflipflop_en_8_q));  // open: q_head
  and and_9 (ram0_6, decoder_2to4_1_o0, dflipflop_en_5_q);
  and and_10 (ram1_6, decoder_2to4_1_o1, dflipflop_en_6_q);
  and and_11 (ram2_6, decoder_2to4_1_o2, dflipflop_en_7_q);
  and and_12 (ram3_6, decoder_2to4_1_o3, dflipflop_en_8_q);
  dflipflop_en dflipflop_en_9 (
    .d(d[5]), .clk(clk), .en(and_2_out), .reset(reset), .q(dflipflop_en_9_q));  // open: q_head
  dflipflop_en dflipflop_en_10 (
    .d(d[5]), .clk(clk), .en(and_3_out), .reset(reset), .q(dflipflop_en_10_q));  // open: q_head
  dflipflop_en dflipflop_en_11 (
    .d(d[5]), .clk(clk), .en(and_1_out), .reset(reset), .q(dflipflop_en_11_q));  // open: q_head
  dflipflop_en dflipflop_en_12 (
    .d(d[5]), .clk(clk), .en(and_4_out), .reset(reset), .q(dflipflop_en_12_q));  // open: q_head
  and and_13 (ram0_5, decoder_2to4_1_o0, dflipflop_en_9_q);
  and and_14 (ram1_5, decoder_2to4_1_o1, dflipflop_en_10_q);
  and and_15 (ram2_5, decoder_2to4_1_o2, dflipflop_en_11_q);
  and and_16 (ram3_5, decoder_2to4_1_o3, dflipflop_en_12_q);
  dflipflop_en dflipflop_en_13 (
    .d(d[4]), .clk(clk), .en(and_2_out), .reset(reset), .q(dflipflop_en_13_q));  // open: q_head
  dflipflop_en dflipflop_en_14 (
    .d(d[4]), .clk(clk), .en(and_3_out), .reset(reset), .q(dflipflop_en_14_q));  // open: q_head
  dflipflop_en dflipflop_en_15 (
    .d(d[4]), .clk(clk), .en(and_1_out), .reset(reset), .q(dflipflop_en_15_q));  // open: q_head
  dflipflop_en dflipflop_en_16 (
    .d(d[4]), .clk(clk), .en(and_4_out), .reset(reset), .q(dflipflop_en_16_q));  // open: q_head
  and and_17 (ram0_4, decoder_2to4_1_o0, dflipflop_en_13_q);
  and and_18 (ram1_4, decoder_2to4_1_o1, dflipflop_en_14_q);
  and and_19 (ram2_4, decoder_2to4_1_o2, dflipflop_en_15_q);
  and and_20 (ram3_4, decoder_2to4_1_o3, dflipflop_en_16_q);
  dflipflop_en dflipflop_en_17 (
    .d(d[3]), .clk(clk), .en(and_2_out), .reset(reset), .q(dflipflop_en_17_q));  // open: q_head
  dflipflop_en dflipflop_en_18 (
    .d(d[3]), .clk(clk), .en(and_3_out), .reset(reset), .q(dflipflop_en_18_q));  // open: q_head
  dflipflop_en dflipflop_en_19 (
    .d(d[3]), .clk(clk), .en(and_1_out), .reset(reset), .q(dflipflop_en_19_q));  // open: q_head
  dflipflop_en dflipflop_en_20 (
    .d(d[3]), .clk(clk), .en(and_4_out), .reset(reset), .q(dflipflop_en_20_q));  // open: q_head
  and and_21 (ram0_3, decoder_2to4_1_o0, dflipflop_en_17_q);
  and and_22 (ram1_3, decoder_2to4_1_o1, dflipflop_en_18_q);
  and and_23 (ram2_3, decoder_2to4_1_o2, dflipflop_en_19_q);
  and and_24 (ram3_3, decoder_2to4_1_o3, dflipflop_en_20_q);
  dflipflop_en dflipflop_en_21 (
    .d(d[2]), .clk(clk), .en(and_2_out), .reset(reset), .q(dflipflop_en_21_q));  // open: q_head
  dflipflop_en dflipflop_en_22 (
    .d(d[2]), .clk(clk), .en(and_3_out), .reset(reset), .q(dflipflop_en_22_q));  // open: q_head
  dflipflop_en dflipflop_en_23 (
    .d(d[2]), .clk(clk), .en(and_1_out), .reset(reset), .q(dflipflop_en_23_q));  // open: q_head
  dflipflop_en dflipflop_en_24 (
    .d(d[2]), .clk(clk), .en(and_4_out), .reset(reset), .q(dflipflop_en_24_q));  // open: q_head
  and and_25 (ram0_2, decoder_2to4_1_o0, dflipflop_en_21_q);
  and and_26 (ram1_2, decoder_2to4_1_o1, dflipflop_en_22_q);
  and and_27 (ram2_2, decoder_2to4_1_o2, dflipflop_en_23_q);
  and and_28 (ram3_2, decoder_2to4_1_o3, dflipflop_en_24_q);
  dflipflop_en dflipflop_en_25 (
    .d(d[1]), .clk(clk), .en(and_2_out), .reset(reset), .q(dflipflop_en_25_q));  // open: q_head
  dflipflop_en dflipflop_en_26 (
    .d(d[1]), .clk(clk), .en(and_3_out), .reset(reset), .q(dflipflop_en_26_q));  // open: q_head
  dflipflop_en dflipflop_en_27 (
    .d(d[1]), .clk(clk), .en(and_1_out), .reset(reset), .q(dflipflop_en_27_q));  // open: q_head
  dflipflop_en dflipflop_en_28 (
    .d(d[1]), .clk(clk), .en(and_4_out), .reset(reset), .q(dflipflop_en_28_q));  // open: q_head
  and and_29 (ram0_1, decoder_2to4_1_o0, dflipflop_en_25_q);
  and and_30 (ram1_1, decoder_2to4_1_o1, dflipflop_en_26_q);
  and and_31 (ram2_1, decoder_2to4_1_o2, dflipflop_en_27_q);
  and and_32 (ram3_1, decoder_2to4_1_o3, dflipflop_en_28_q);
  dflipflop_en dflipflop_en_29 (
    .d(d[0]), .clk(clk), .en(and_2_out), .reset(reset), .q(dflipflop_en_29_q));  // open: q_head
  dflipflop_en dflipflop_en_30 (
    .d(d[0]), .clk(clk), .en(and_3_out), .reset(reset), .q(dflipflop_en_30_q));  // open: q_head
  dflipflop_en dflipflop_en_31 (
    .d(d[0]), .clk(clk), .en(and_1_out), .reset(reset), .q(dflipflop_en_31_q));  // open: q_head
  dflipflop_en dflipflop_en_32 (
    .d(d[0]), .clk(clk), .en(and_4_out), .reset(reset), .q(dflipflop_en_32_q));  // open: q_head
  and and_33 (ram0_0, decoder_2to4_1_o0, dflipflop_en_29_q);
  and and_34 (ram1_0, decoder_2to4_1_o1, dflipflop_en_30_q);
  and and_35 (ram2_0, decoder_2to4_1_o2, dflipflop_en_31_q);
  and and_36 (ram3_0, decoder_2to4_1_o3, dflipflop_en_32_q);
endmodule
