// Logisim project reg.circ as structural Verilog: 1 circuit, main circuit reg4bit
module reg4bit (
  input  [3:0] d,
  input  en,
  input  clk,
  input  reset,
  output [3:0] q
);

  dflipflop_en dflipflop_en_1 (.d(d[0]), .clk(clk), .en(en), .reset(reset), .q(q[0]));  // open: q_head
  dflipflop_en dflipflop_en_2 (.d(d[1]), .clk(clk), .en(en), .reset(reset), .q(q[1]));  // open: q_head
  dflipflop_en dflipflop_en_3 (.d(d[2]), .clk(clk), .en(en), .reset(reset), .q(q[2]));  // open: q_head
  dflipflop_en dflipflop_en_4 (.d(d[3]), .clk(clk), .en(en), .reset(reset), .q(q[3]));  // open: q_head
endmodule
