// Logisim project rom8x8.circ as structural Verilog: 1 circuit, main circuit rom_8x8
module rom_8x8 (
  input  [3:0] addr,
  output [7:0] out_2
);

  wire and_1_out, and_2_out, and_3_out, and_4_out, and_5_out, and_6_out, and_7_out, and_8_out, and_9_out,
       and_10_out, and_11_out, and_12_out, and_13_out, and_14_out, and_15_out, and_16_out, and_17_out,
       and_18_out, and_19_out, and_20_out, and_21_out, and_22_out, and_23_out, and_24_out, and_25_out,
       and_26_out, and_27_out, and_28_out, and_29_out, and_30_out, and_31_out, and_32_out, and_33_out,
       and_34_out, and_35_out, and_36_out, and_37_out, and_38_out, and_39_out, and_40_out, and_41_out,
       and_42_out, and_43_out, and_44_out, and_45_out, and_46_out, and_47_out, and_48_out, and_49_out,
       and_50_out, and_51_out, and_52_out, and_53_out, and_54_out, and_55_out, and_56_out, and_57_out,
       and_58_out, and_59_out, and_60_out, and_61_out, and_62_out, and_63_out, and_64_out,
       decoder_4to16_1_o0, decoder_4to16_1_o1, decoder_4to16_1_o2, decoder_4to16_1_o3, decoder_4to16_1_o4,
       decoder_4to16_1_o5, decoder_4to16_1_o6, decoder_4to16_1_o7;

  decoder_4to16 decoder_4to16_1 (
    .i0(addr[0]), .i1(addr[1]), .i2(addr[2]), .i3(addr[3]), .o0(decoder_4to16_1_o0), .o1(decoder_4to16_1_o1),
    .o2(decoder_4to16_1_o2), .o3(decoder_4to16_1_o3), .o4(decoder_4to16_1_o4), .o5(decoder_4to16_1_o5),
    .o6(decoder_4to16_1_o6), .o7(decoder_4to16_1_o7));  // open: o8, o9, o10, o11, o12, o13, o14, o15
  and and_1 (and_1_out, decoder_4to16_1_o0, 1'b1);
  and and_2 (and_2_out, decoder_4to16_1_o1, 1'b1);
  and and_3 (and_3_out, decoder_4to16_1_o2, 1'b1);
  and and_4 (and_4_out, decoder_4to16_1_o3, 1'b1);
  and and_5 (and_5_out, decoder_4to16_1_o4, 1'b0);
  and and_6 (and_6_out, decoder_4to16_1_o5, 1'b0);
  and and_7 (and_7_out, decoder_4to16_1_o6, 1'b1);
  and and_8 (and_8_out, decoder_4to16_1_o7, 1'b1);
  or or_1 (out_2[7], and_1_out, and_2_out, and_3_out, and_4_out, and_5_out, and_6_out, and_7_out, and_8_out);
  and and_9 (and_9_out, decoder_4to16_1_o0, 1'b0);
  and and_10 (and_10_out, decoder_4to16_1_o1, 1'b0);
  and and_11 (and_11_out, decoder_4to16_1_o2, 1'b0);
  and and_12 (and_12_out, decoder_4to16_1_o3, 1'b0);
  and and_13 (and_13_out, decoder_4to16_1_o4, 1'b0);
  and and_14 (and_14_out, decoder_4to16_1_o5, 1'b0);
  and and_15 (and_15_out, decoder_4to16_1_o6, 1'b1);
  and and_16 (and_16_out, decoder_4to16_1_o7, 1'b1);
  or or_2 (out_2[6], and_9_out, and_10_out, and_11_out, and_12_out, and_13_out, and_14_out, and_15_out, and_16_out);
  and and_17 (and_17_out, decoder_4to16_1_o0, 1'b0);
  and and_18 (and_18_out, decoder_4to16_1_o1, 1'b0);
  and and_19 (and_19_out, decoder_4to16_1_o2, 1'b1);
  and and_20 (and_20_out, decoder_4to16_1_o3, 1'b1);
  and and_21 (and_21_out, decoder_4to16_1_o4, 1'b0);
  and and_22 (and_22_out, decoder_4to16_1_o5, 1'b1);
  and and_23 (and_23_out, decoder_4to16_1_o6, 1'b0);
  and and_24 (and_24_out, decoder_4to16_1_o7, 1'b0);
  or or_3 (out_2[5], and_17_out, and_18_out, and_19_out, and_20_out, and_21_out, and_22_out, and_23_out, and_24_out);
  and and_25 (and_25_out, decoder_4to16_1_o0, 1'b0);
  and and_26 (and_26_out, decoder_4to16_1_o1, 1'b1);
  and and_27 (and_27_out, decoder_4to16_1_o2, 1'b0);
  and and_28 (and_28_out, decoder_4to16_1_o3, 1'b1);
  and and_29 (and_29_out, decoder_4to16_1_o4, 1'b1);
  and and_30 (and_30_out, decoder_4to16_1_o5, 1'b0);
  and and_31 (and_31_out, decoder_4to16_1_o6, 1'b1);
  and and_32 (and_32_out, decoder_4to16_1_o7, 1'b1);
  or or_4 (out_2[4], and_25_out, and_26_out, and_27_out, and_28_out, and_29_out, and_30_out, and_31_out, and_32_out);
  and and_33 (and_33_out, decoder_4to16_1_o0, 1'b1);
  and and_34 (and_34_out, decoder_4to16_1_o1, 1'b0);
  and and_35 (and_35_out, decoder_4to16_1_o2, 1'b0);
  and and_36 (and_36_out, decoder_4to16_1_o3, 1'b0);
  and and_37 (and_37_out, decoder_4to16_1_o4, 1'b0);
  and and_38 (and_38_out, decoder_4to16_1_o5, 1'b1);
  and and_39 (and_39_out, decoder_4to16_1_o6, 1'b0);
  and and_40 (and_40_out, decoder_4to16_1_o7, 1'b1);
  or or_5 (out_2[3], and_33_out, and_34_out, and_35_out, and_36_out, and_37_out, and_38_out, and_39_out, and_40_out);
  and and_41 (and_41_out, decoder_4to16_1_o0, 1'b0);
  and and_42 (and_42_out, decoder_4to16_1_o1, 1'b0);
  and and_43 (and_43_out, decoder_4to16_1_o2, 1'b0);
  and and_44 (and_44_out, decoder_4to16_1_o3, 1'b0);
  and and_45 (and_45_out, decoder_4to16_1_o4, 1'b1);
  and and_46 (and_46_out, decoder_4to16_1_o5, 1'b0);
  and and_47 (and_47_out, decoder_4to16_1_o6, 1'b0);
  and and_48 (and_48_out, decoder_4to16_1_o7, 1'b1);
  or or_6 (out_2[2], and_41_out, and_42_out, and_43_out, and_44_out, and_45_out, and_46_out, and_47_out, and_48_out);
  and and_49 (and_49_out, decoder_4to16_1_o0, 1'b1);
  and and_50 (and_50_out, decoder_4to16_1_o1, 1'b0);
  and and_51 (and_51_out, decoder_4to16_1_o2, 1'b0);
  and and_52 (and_52_out, decoder_4to16_1_o3, 1'b0);
  and and_53 (and_53_out, decoder_4to16_1_o4, 1'b1);
  and and_54 (and_54_out, decoder_4to16_1_o5, 1'b0);
  and and_55 (and_55_out, decoder_4to16_1_o6, 1'b0);
  and and_56 (and_56_out, decoder_4to16_1_o7, 1'b1);
  or or_7 (out_2[1], and_49_out, and_50_out, and_51_out, and_52_out, and_53_out, and_54_out, and_55_out, and_56_out);
  and and_57 (and_57_out, decoder_4to16_1_o0, 1'b0);
  and and_58 (and_58_out, decoder_4to16_1_o1, 1'b0);
  and and_59 (and_59_out, decoder_4to16_1_o2, 1'b0);
  and and_60 (and_60_out, decoder_4to16_1_o3, 1'b1);
  and and_61 (and_61_out, decoder_4to16_1_o4, 1'b1);
  and and_62 (and_62_out, decoder_4to16_1_o5, 1'b1);
  and and_63 (and_63_out, decoder_4to16_1_o6, 1'b1);
  and and_64 (and_64_out, decoder_4to16_1_o7, 1'b1);
  or or_8 (out_2[0], and_57_out, and_58_out, and_59_out, and_60_out, and_61_out, and_62_out, and_63_out, and_64_out);
endmodule
