// Logisim project srlatch.circ as structural Verilog: 1 circuit, main circuit srlatch
module srlatch (
  input  r,
  input  s,
  output q,
  output q_head
);

  wire or_1_out, or_2_out;

  or or_1 (or_1_out, r, q_head);
  or or_2 (or_2_out, q, s);
  not not_1 (q, or_1_out);
  not not_2 (q_head, or_2_out);

  // Notes on the sheet:
  //   r: initial=0x1
endmodule
