// Logisim project sumnumsequence.circ as structural Verilog: 1 circuit, main circuit main
module main (
  input  in_1,
  input  in_2,
  input  in_3,
  output [7:0] out_4
);

  wire [7:0] adder8bit_1_s, reg8bit_1_q, reg8bit_2_q;

  reg8bit reg8bit_1 (.d(adder8bit_1_s), .en(in_1), .clk(in_2), .reset(in_3), .q(reg8bit_1_q));
  adder8bit adder8bit_1 (.a(reg8bit_1_q), .b(8'h1), .cin(1'b0), .s(adder8bit_1_s));  // open: overflow, cout
  reg8bit reg8bit_2 (.d(out_4), .en(in_1), .clk(in_2), .reset(in_3), .q(reg8bit_2_q));
  adder8bit adder8bit_2 (.a(reg8bit_2_q), .b(adder8bit_1_s), .cin(1'b0), .s(out_4));  // open: overflow, cout
  // Probe on out_4
endmodule
