// Logisim project xnor_transitor.circ as structural Verilog: 1 circuit, main circuit main
module main (
  input  a,
  input  b,
  output out_3
);

  wire transistor_1_out;

  Transistor transistor_1 (.in(1'b1), .out(transistor_1_out), .gate(a));
  Transistor #(.\type ("n")) transistor_2 (.in(1'b0), .out(transistor_1_out), .gate(a));
  Transistor transistor_3 (.in(transistor_1_out), .out(out_3), .gate(b));
  Transistor #(.\type ("n")) transistor_4 (.in(a), .out(out_3), .gate(b));
  // Transmission_Gate transmission_1: pin names not known; wires that end beside it: b, transistor_1_out, a, out_3
endmodule
